# Fritzing sketch Schema Fritzing (saved by Fritzing 0.8.7b)
breadboards: 1

parts:
  Arduino_Leonardo = Arduino Leonardo (Rev3b)
  U1 = Voltage Regulator - Variable [package="TO220 [THT]"]
  Module_Bluetooth_HC-05 = Bluetooth Mate Silver
  BAT1 = BC9VPC [package=bc9vpc]
  Interrupteur_Moteurs = Toggle Switch [package=THT]
  Interrupteur_Arduino = Toggle Switch [package=THT]
  R1 = Resistor [tolerance=±5% resistance=220 package=THT]
  IC1 = L293D [package=THT]
  R3 = Resistor [tolerance=±5% resistance=220 package=THT]
  R4 = Resistor [tolerance=±5% resistance=220 package=THT]
  C2 = Capacitor [package=cap-pth-small2]
  C3 = Capacitor [package=cap-pth-small2]
  Moteur_Droite = DC Motor
  Moteur_Gauche = DC Motor
  C4 = Ceramic Capacitor [capacitance="100 nF" package="0603 [SMD, multilayer]"]
  Power_Jack_pour_alimentation_externe = Audio Jack (TRRS) 3.5mm [package="RC-5325A [SMD]"]

nets:
  N1: Arduino_Leonardo.D0/RX, Module_Bluetooth_HC-05.VCC
  N2: Arduino_Leonardo.D1/TX, R1.Pin_0, R3.Pin_1
  N3: Arduino_Leonardo.D2/SDA, IC1.Enable_2
  N4: Arduino_Leonardo.D5_PWM, IC1.In_1
  N5: Arduino_Leonardo.D6_PWM/A7, IC1.In_2
  N6: Arduino_Leonardo.3V3, Module_Bluetooth_HC-05.RX_5V
  N7: Arduino_Leonardo.GND, U1.OUT, Module_Bluetooth_HC-05.TX_5V, IC1.0V, C2.2, C3.2, C4.1, Power_Jack_pour_alimentation_externe.SLEEVE
  N8: Arduino_Leonardo.D9_PWM/A9, IC1.In_4
  N9: Arduino_Leonardo.D10_PWM/A10, IC1.In_3
  N10: U1.ADJ, Interrupteur_Moteurs.COM, C4.0
  N11: U1.IN, IC1.+V
  N12: Module_Bluetooth_HC-05.CTS_5V, R1.Pin_1
  N13: BAT1.V+, Interrupteur_Arduino.COM
  N14: Interrupteur_Moteurs.L1, Power_Jack_pour_alimentation_externe.TIP
  N15: IC1.Out_1_(_Controlled_by_Enable_1_), C3.1, Moteur_Droite.pin_2
  N16: IC1.Out_2_(_Controlled_by_Enable_1_), Moteur_Droite.pin_1
  N17: IC1.Out_3_(_Controlled_by_Enable_2_), Moteur_Gauche.pin_2
  N18: IC1.Out_4_(_Controlled_by_Enable_2_), C2.1, Moteur_Gauche.pin_1
  N19: R3.Pin_0, R4.Pin_0

notes:
  Schéma Fritzing du circuit
